# Fritzing sketch pot_servo_schematic (saved by Fritzing 0.9.3b)
breadboards: 1

parts:
  Part1 = Arduino Uno (Rev3)
  IC2 = Voltage Regulator [package=to220-igo]
  VCC1 = Battery block 9V
  J1 = Basic Servo
  R1 = Rotary Potentiometer (Small) [maximum_resistance=100kΩ package=THT]

nets:
  N1: Part1.A0, R1.wiper
  N2: Part1.D9_PWM, J1.pulse
  N3: Part1.5V, R1.leg2
  GND: Part1.GND, IC2.IN, VCC1.-, J1.gnd, R1.leg1
  N4: IC2.GND, VCC1.+
  N5: IC2.OUT, J1.vcc
